# Fritzing sketch battery_led (saved by Fritzing 1.0.8)
circuit board: 7.5000cm x 5.6000cm
breadboards: 1

parts:
  BT1 = 4 x AAA Battery Mount
  SW1 = Pushbutton [package=THT]
  R1 = Resistor [tolerance=±5% resistance=330 power=0.25W package=THT]
  D1 = LED - 5mm [color="Red (633nm)" current=0.030A package="5 mm [THT]"]

nets:
  N1: BT1.-, D1.cathode
  N2: BT1.+, SW1.leg1
  N3: SW1.leg0, R1.Pin_0
  N4: R1.Pin_1, D1.anode
