# Fritzing sketch header_led (saved by Fritzing 1.0.8)
circuit board: 4.0000cm x 2.6000cm
breadboards: 1

parts:
  J1 = Power header 2-pin (+5V, GND)
  R1 = Resistor [tolerance=±5% resistance=330 power=0.25W package=THT]
  D1 = LED - 5mm [color="Red (633nm)" current=0.030A package="5 mm [THT]"]

nets:
  N1: J1.+5V, R1.Pin_0
  N2: J1.GND, D1.cathode
  N3: R1.Pin_1, D1.anode

custom parts:
  Power header 2-pin (+5V, GND): 2-pin 0.1 in header; pin 1 is +5V, pin 2 is GND. Made by the fritzing skill example script.
